// Logisim project 8bit_cpu.circ as structural Verilog: 9 circuits, main circuit main
module main (
  input  enable,
  input  [3:0] OE_data_testing,
  input  [7:0] Testing_data,
  input  Testing_enable,
  input  counter_enable,
  output [3:0] content_of_counter,
  output [3:0] MAR_content,
  output [7:0] IR_content,
  output [7:0] MBR_content,
  output [7:0] Register_A_data,
  output [7:0] ALU_outpot,
  output [7:0] out_12,
  output [7:0] Register_B_data,
  output [2:0] out_14
);

  wire C0, C1, C2, C3, C4, C5, C6, C7, C8, C9, C10, C11, C12, C13, C14, C15, clock;
  wire [3:0] bitselector_2_out, controlled_buffer_1_out, mem_add_sto_mar_1_o;
  wire [7:0] address, ALU_output, bit_extender_2_out, Instruction_register_o;
  wire [31:0] n7seg_1_out_2, n7seg_2_out_2, n7seg_3_out_2, n7seg_4_out_2, n7seg_5_out_2;

  _7seg u_7seg_1 (.Din(Register_A_data), .out_2(n7seg_1_out_2));
  _7seg u_7seg_2 (.Din(Register_B_data), .out_2(n7seg_2_out_2));
  _7seg u_7seg_3 (.Din(address), .out_2(n7seg_3_out_2));
  _7_Segment_Display u_7_segment_display_1 (
    .g(n7seg_1_out_2[11]), .f(n7seg_1_out_2[10]), .a(n7seg_1_out_2[9]), .b(n7seg_1_out_2[8]),
    .e(n7seg_1_out_2[27]), .d(n7seg_1_out_2[26]), .c(n7seg_1_out_2[25]), .dp(n7seg_1_out_2[24]));
  _7_Segment_Display u_7_segment_display_2 (
    .g(n7seg_2_out_2[11]), .f(n7seg_2_out_2[10]), .a(n7seg_2_out_2[9]), .b(n7seg_2_out_2[8]),
    .e(n7seg_2_out_2[27]), .d(n7seg_2_out_2[26]), .c(n7seg_2_out_2[25]), .dp(n7seg_2_out_2[24]));
  _7_Segment_Display u_7_segment_display_3 (
    .g(n7seg_3_out_2[3]), .f(n7seg_3_out_2[2]), .a(n7seg_3_out_2[1]), .b(n7seg_3_out_2[0]),
    .e(n7seg_3_out_2[19]), .d(n7seg_3_out_2[18]), .c(n7seg_3_out_2[17]), .dp(n7seg_3_out_2[16]));
  _7_Segment_Display u_7_segment_display_4 (
    .g(n7seg_1_out_2[7]), .f(n7seg_1_out_2[6]), .a(n7seg_1_out_2[5]), .b(n7seg_1_out_2[4]),
    .e(n7seg_1_out_2[23]), .d(n7seg_1_out_2[22]), .c(n7seg_1_out_2[21]), .dp(n7seg_1_out_2[20]));
  _7_Segment_Display u_7_segment_display_5 (
    .g(n7seg_1_out_2[3]), .f(n7seg_1_out_2[2]), .a(n7seg_1_out_2[1]), .b(n7seg_1_out_2[0]),
    .e(n7seg_1_out_2[19]), .d(n7seg_1_out_2[18]), .c(n7seg_1_out_2[17]), .dp(n7seg_1_out_2[16]));
  _7_Segment_Display u_7_segment_display_6 (
    .g(n7seg_2_out_2[3]), .f(n7seg_2_out_2[2]), .a(n7seg_2_out_2[1]), .b(n7seg_2_out_2[0]),
    .e(n7seg_2_out_2[19]), .d(n7seg_2_out_2[18]), .c(n7seg_2_out_2[17]), .dp(n7seg_2_out_2[16]));
  _7_Segment_Display u_7_segment_display_7 (
    .g(n7seg_2_out_2[7]), .f(n7seg_2_out_2[6]), .a(n7seg_2_out_2[5]), .b(n7seg_2_out_2[4]),
    .e(n7seg_2_out_2[23]), .d(n7seg_2_out_2[22]), .c(n7seg_2_out_2[21]), .dp(n7seg_2_out_2[20]));
  Counter #(.width(4), .max('h3)) counter_1 (
    .D(controlled_buffer_1_out), .count(C1), .Q(content_of_counter), .clk(clock));  // open: load, carry, clr
  Clock clock_1 (.out(clock));
  assign controlled_buffer_1_out = C0 ? content_of_counter : 4'bz;  // Controlled_Buffer controlled_buffer_1
  assign address = {{4{1'b0}}, content_of_counter};  // Bit_Extender bit_extender_1
  CPU_mem_8 Instruction_register (
    .o(Instruction_register_o), .c(clock), .s(C7), .i(ALU_output), .e(C8), .STORAGE(IR_content));  // open: r
  CPU_mem_8 register_A (.c(clock), .s(C12), .i(ALU_output), .STORAGE(Register_A_data));  // open: o, e, r
  CPU_mem_8 register_B (.c(clock), .s(C13), .i(ALU_output), .STORAGE(Register_B_data));  // open: o, e, r
  BitSelector #(.group(4)) bitselector_1 (.in(Instruction_register_o), .out(controlled_buffer_1_out), .sel(1'b0));
  ALU ALU (
    .A(Register_A_data), .B(Register_B_data), .alu_data(ALU_outpot), .in_3(C11), .\output (ALU_output));  // open: COUT
  LED D7 (.in(ALU_output[7]));
  assign ALU_output = Testing_enable ? Testing_data : 8'bz;  // Controlled_Buffer controlled_buffer_2
  LED D4 (.in(ALU_output[4]));
  LED D3 (.in(ALU_output[3]));
  LED D6 (.in(ALU_output[6]));
  LED D5 (.in(ALU_output[5]));
  LED D1 (.in(ALU_output[1]));
  LED D2 (.in(ALU_output[2]));
  LED D0 (.in(ALU_output[0]));
  Mem_add_sto_MAR mem_add_sto_mar_1 (
    .o(mem_add_sto_mar_1_o), .i(controlled_buffer_1_out), .STORAGE(MAR_content), .e(C10), .s(C9), .c(clock));  // open: r
  assign ALU_output = C5 ? MBR_content : 8'bz;  // Controlled_Buffer controlled_buffer_3
  _7seg u_7seg_4 (.Din(out_12), .out_2(n7seg_4_out_2));
  CPU_mem_8 MBR (.o(ALU_output), .c(clock), .s(C4), .i(ALU_output), .e(C6), .STORAGE(MBR_content));  // open: r
  _7_Segment_Display u_7_segment_display_8 (
    .g(n7seg_4_out_2[11]), .f(n7seg_4_out_2[10]), .a(n7seg_4_out_2[9]), .b(n7seg_4_out_2[8]),
    .e(n7seg_4_out_2[27]), .d(n7seg_4_out_2[26]), .c(n7seg_4_out_2[25]), .dp(n7seg_4_out_2[24]));
  CPU_mem_8 output_register (.o(ALU_output), .c(clock), .s(C15), .i(ALU_output), .e(C14), .STORAGE(out_12));  // open: r
  _7_Segment_Display u_7_segment_display_9 (
    .g(n7seg_4_out_2[7]), .f(n7seg_4_out_2[6]), .a(n7seg_4_out_2[5]), .b(n7seg_4_out_2[4]),
    .e(n7seg_4_out_2[23]), .d(n7seg_4_out_2[22]), .c(n7seg_4_out_2[21]), .dp(n7seg_4_out_2[20]));
  _7_Segment_Display u_7_segment_display_10 (
    .g(n7seg_4_out_2[3]), .f(n7seg_4_out_2[2]), .a(n7seg_4_out_2[1]), .b(n7seg_4_out_2[0]),
    .e(n7seg_4_out_2[19]), .d(n7seg_4_out_2[18]), .c(n7seg_4_out_2[17]), .dp(n7seg_4_out_2[16]));
  assign mem_add_sto_mar_1_o = enable ? OE_data_testing : 4'bz;  // Controlled_Buffer controlled_buffer_4
  LED D7_2 (.in(ALU_output[7]));
  LED D5_2 (.in(ALU_output[5]));
  LED D4_2 (.in(ALU_output[4]));
  LED D3_2 (.in(ALU_output[3]));
  LED D6_2 (.in(ALU_output[6]));
  LED D0_2 (.in(ALU_output[0]));
  LED D2_2 (.in(ALU_output[2]));
  LED D1_2 (.in(ALU_output[1]));
  BitSelector #(.group(4)) bitselector_2 (.in(IR_content), .out(bitselector_2_out), .sel(1'b1));
  Counter #(.width(3), .max('h5)) counter_2 (
    .count(counter_enable), .Q(out_14), .clk(clock));  // open: load, D, carry, clr
  RAM #(.addrWidth(4), .bus("separate")) ram_1 (
    .addr(mem_add_sto_mar_1_o), .din(ALU_output), .data(ALU_output), .str(C2), .clk(clock), .ld(C3));  // open: sel, clr
  cu1 cu1_1 (
    .OPC3(bitselector_2_out[3]), .OPC2(bitselector_2_out[2]), .OPC1(bitselector_2_out[1]),
    .OPC0(bitselector_2_out[0]), .SC2(out_14[2]), .SC1(out_14[1]), .SC0(out_14[0]), .C0(C0), .C1(C1),
    .C2(C2), .C3(C3), .C4(C4), .C5(C5), .C6(C6), .C7(C7), .C8(C8), .C9(C9), .C10(C10), .C11(C11));
  CU2 cu2_1 (
    .OPC3(bitselector_2_out[3]), .OPC2(bitselector_2_out[2]), .OPC1(bitselector_2_out[1]),
    .OPC0(bitselector_2_out[0]), .SC2(out_14[2]), .SC1(out_14[1]), .SC0(out_14[0]), .C12(C12), .C13(C13),
    .C14(C14), .C15(C15));
  _7seg u_7seg_5 (.Din(bit_extender_2_out), .out_2(n7seg_5_out_2));
  assign bit_extender_2_out = {{5{1'b0}}, out_14};  // Bit_Extender bit_extender_2
  _7_Segment_Display u_7_segment_display_11 (
    .g(n7seg_5_out_2[3]), .f(n7seg_5_out_2[2]), .a(n7seg_5_out_2[1]), .b(n7seg_5_out_2[0]),
    .e(n7seg_5_out_2[19]), .d(n7seg_5_out_2[18]), .c(n7seg_5_out_2[17]), .dp(n7seg_5_out_2[16]));

  // Other names for the same wires on the sheet: A_content[7:0] = Register_A_data; B_content[7:0] = Register_B_data;
  //   output_content[7:0] = out_12

  // Notes on the sheet:
  //   internal address bus(4bit)
  //   Internal Data Bus
  //   external address bus(4bit)
  //   external Data Bus
  //   step counter
endmodule

module CPU_mem_8 (
  input  r,
  input  e,
  input  s,
  input  c,
  input  [7:0] i,
  output [7:0] o,
  output [7:0] STORAGE
);

  CPU_mem_1 cpu_mem_1_1 (.clock(c), .save(s), .b_in(i[0]), .e(e), .reset(r), .b_out(o[0]), .stored_b(STORAGE[0]));
  CPU_mem_1 cpu_mem_1_2 (.clock(c), .save(s), .b_in(i[1]), .e(e), .reset(r), .b_out(o[1]), .stored_b(STORAGE[1]));
  CPU_mem_1 cpu_mem_1_3 (.clock(c), .save(s), .b_in(i[2]), .e(e), .reset(r), .b_out(o[2]), .stored_b(STORAGE[2]));
  CPU_mem_1 cpu_mem_1_4 (.clock(c), .save(s), .b_in(i[3]), .e(e), .reset(r), .b_out(o[3]), .stored_b(STORAGE[3]));
  CPU_mem_1 cpu_mem_1_5 (.clock(c), .save(s), .b_in(i[4]), .e(e), .reset(r), .b_out(o[4]), .stored_b(STORAGE[4]));
  CPU_mem_1 cpu_mem_1_6 (.clock(c), .save(s), .b_in(i[5]), .e(e), .reset(r), .b_out(o[5]), .stored_b(STORAGE[5]));
  CPU_mem_1 cpu_mem_1_7 (.clock(c), .save(s), .b_in(i[6]), .e(e), .reset(r), .b_out(o[6]), .stored_b(STORAGE[6]));
  CPU_mem_1 cpu_mem_1_8 (.clock(c), .save(s), .b_in(i[7]), .e(e), .reset(r), .b_out(o[7]), .stored_b(STORAGE[7]));

  // Other names for the same wires on the sheet: _0 = i[0]; _1 = i[1]; _2 = i[2]; _3 = i[3]; _4 = i[4]; _5 = i[5];
  //   _6 = i[6]; _7 = i[7]; A = STORAGE[0]; B = STORAGE[1]; C_t = STORAGE[2]; D = STORAGE[3]; E_t = STORAGE[4];
  //   F = STORAGE[5]; G = STORAGE[6]; H = STORAGE[7]
endmodule

module CPU_mem_1 (
  input  clock,
  input  save,
  input  b_in,
  input  e,
  input  reset,
  output b_out,
  output stored_b
);

  wire and_1_out, and_2_out, not_1_out, or_1_out;

  not not_1 (not_1_out, save);
  and and_1 (and_1_out, stored_b, not_1_out);
  and and_2 (and_2_out, save, b_in);
  or or_1 (or_1_out, and_1_out, and_2_out);
  D_Flip_Flop d_ff_1 (.clk(clock), .D(or_1_out), .Q(stored_b), .reset(reset));  // open: Qn, preset, en
  assign b_out = e ? stored_b : 1'bz;  // Controlled_Buffer controlled_buffer_1
endmodule

module Mem_add_sto_MAR (
  input  [3:0] i,
  input  r,
  input  e,
  input  s,
  input  c,
  output [3:0] o,
  output [3:0] STORAGE
);

  CPU_mem_1 cpu_mem_1_1 (.clock(c), .save(s), .b_in(i[0]), .e(e), .reset(r), .b_out(o[0]), .stored_b(STORAGE[0]));
  CPU_mem_1 cpu_mem_1_2 (.clock(c), .save(s), .b_in(i[1]), .e(e), .reset(r), .b_out(o[1]), .stored_b(STORAGE[1]));
  CPU_mem_1 cpu_mem_1_3 (.clock(c), .save(s), .b_in(i[2]), .e(e), .reset(r), .b_out(o[2]), .stored_b(STORAGE[2]));
  CPU_mem_1 cpu_mem_1_4 (.clock(c), .save(s), .b_in(i[3]), .e(e), .reset(r), .b_out(o[3]), .stored_b(STORAGE[3]));

  // Other names for the same wires on the sheet: A = STORAGE[0]; B = STORAGE[1]; C_t = STORAGE[2]; D = STORAGE[3]
endmodule

module ALU (
  input  [7:0] A,
  input  [7:0] B,
  input  in_3,
  output [7:0] \output ,
  output [7:0] alu_data,
  output COUT
);

  Adder adder_1 (.a(A), .b(B), .out(alu_data), .cout(COUT));  // open: cin
  assign \output  = in_3 ? alu_data : 8'bz;  // Controlled_Buffer controlled_buffer_1
endmodule

module ruf (
  input  [7:0] in_1,
  input  [3:0] in_2,
  input  in_3,
  input  [7:0] in_4,
  input  in_5,
  input  in_6,
  input  in_7,
  input  in_8,
  input  in_9,
  input  [7:0] in_10,
  input  in_11,
  input  [7:0] Din,
  input  [3:0] Din_2,
  output [7:0] out_14,
  output [7:0] out_15,
  output [7:0] out_16,
  output [2:0] out_17
);

  wire clock_1_out, clock_2_out;
  wire [3:0] rom_1_data_2;
  wire [7:0] bit_extender_1_out;
  wire [15:0] rom_3_data;
  wire [31:0] n7seg_1_out_2, rom_1_data, rom_2_data;

  ROM #(.dataWidth(32)) rom_1 (.addr(Din), .data({rom_1_data[31:8], rom_1_data_2, rom_1_data[3:0]}));  // open: sel
  ROM #(.dataWidth(32)) rom_2 (.addr(in_10), .data(rom_2_data));  // open: sel
  ROM #(.addrWidth(4), .dataWidth(16)) rom_3 (.addr(Din_2), .data(rom_3_data));  // open: sel
  CPU_mem_8 cpu_mem_8_1 (.o(out_14), .c(in_3), .s(in_5), .i(in_1), .e(in_9), .r(in_8), .STORAGE(out_16));
  _7_Segment_Display u_7_segment_display_1 (
    .g(rom_2_data[19]), .f(rom_2_data[18]), .a(rom_2_data[17]), .b(rom_2_data[16]), .e(rom_2_data[23]),
    .d(rom_2_data[22]), .c(rom_2_data[21]), .dp(rom_2_data[20]));
  _7_Segment_Display u_7_segment_display_2 (
    .g(rom_3_data[3]), .f(rom_3_data[2]), .a(rom_3_data[1]), .b(rom_3_data[0]), .e(rom_3_data[7]),
    .d(rom_3_data[6]), .c(rom_3_data[5]), .dp(rom_3_data[4]));
  _7_Segment_Display u_7_segment_display_3 (
    .g(rom_3_data[11]), .f(rom_3_data[10]), .a(rom_3_data[9]), .b(rom_3_data[8]), .e(rom_3_data[15]),
    .d(rom_3_data[14]), .c(rom_3_data[13]), .dp(rom_3_data[12]));
  _7_Segment_Display u_7_segment_display_4 (
    .g(rom_2_data[11]), .f(rom_2_data[10]), .a(rom_2_data[9]), .b(rom_2_data[8]), .e(rom_2_data[15]),
    .d(rom_2_data[14]), .c(rom_2_data[13]), .dp(rom_2_data[12]));
  _7_Segment_Display u_7_segment_display_5 (
    .g(rom_2_data[3]), .f(rom_2_data[2]), .a(rom_2_data[1]), .b(rom_2_data[0]), .e(rom_2_data[7]),
    .d(rom_2_data[6]), .c(rom_2_data[5]), .dp(rom_2_data[4]));
  _7_Segment_Display u_7_segment_display_6 (
    .g(rom_1_data[19]), .f(rom_1_data[18]), .a(rom_1_data[17]), .b(rom_1_data[16]), .e(rom_1_data[23]),
    .d(rom_1_data[22]), .c(rom_1_data[21]), .dp(rom_1_data[20]));
  _7_Segment_Display u_7_segment_display_7 (
    .g(rom_1_data[3]), .f(rom_1_data[2]), .a(rom_1_data[1]), .b(rom_1_data[0]), .e(rom_1_data_2[3]),
    .d(rom_1_data_2[2]), .c(rom_1_data_2[1]), .dp(rom_1_data_2[0]));
  _7_Segment_Display u_7_segment_display_8 (
    .g(rom_1_data[11]), .f(rom_1_data[10]), .a(rom_1_data[9]), .b(rom_1_data[8]), .e(rom_1_data[15]),
    .d(rom_1_data[14]), .c(rom_1_data[13]), .dp(rom_1_data[12]));
  Clock clock_1 (.out(clock_1_out));
  RAM #(.addrWidth(4), .bus("separate")) ram_1 (
    .addr(in_2), .din(in_4), .data(out_15), .str(in_6), .clk(clock_1_out), .ld(in_7));  // open: sel, clr
  Counter #(.width(3), .max('h5)) counter_1 (
    .count(in_11), .Q(out_17), .clk(clock_2_out));  // open: load, D, carry, clr
  Clock clock_2 (.out(clock_2_out));
  assign bit_extender_1_out = {{5{1'b0}}, out_17};  // Bit_Extender bit_extender_1
  _7seg u_7seg_1 (.Din(bit_extender_1_out), .out_2(n7seg_1_out_2));
  _7_Segment_Display u_7_segment_display_9 (
    .g(n7seg_1_out_2[3]), .f(n7seg_1_out_2[2]), .a(n7seg_1_out_2[1]), .b(n7seg_1_out_2[0]),
    .e(n7seg_1_out_2[19]), .d(n7seg_1_out_2[18]), .c(n7seg_1_out_2[17]), .dp(n7seg_1_out_2[16]));

  // Notes on the sheet:
  //   contents of rom_1 (hex, n*v repeats v):
  //   e7 21 cb 6b 2d 6e ee 23 ef 2f 21e7 2121 21cb 216b 212d 216e 21ee 2123 21ef 212f cbe7 cb21 cbcb cb6b
  //   cb2d cb6e cbee cb23 cbef cb2f 6be7 6b21 6bcb 6b6b 6b2d 6b6e 6bee 6b23 6bef 6b2f 2de7 2d21 2dcb 2d6b
  //   2d2d 2d6e 2dee 2d23 2def 2d2f 6ee7 6e21 6ecb 6e6b 6e2d 6e6e 6eee 6e23 6eef 6e2f eee7 ee21 eecb ee6b
  //   ee2d ee6e eeee ee23 eeef ee2f 23e7 2321 23cb 236b 232d 236e 23ee 2323 23ef 232f efe7 ef21 efcb ef6b
  //   ef2d ef6e efee ef23 efef ef2f 2fe7 2f21 2fcb 2f6b 2f2d 2f6e 2fee 2f23 2fef 2f2f 21e7e7 21e721 21e7cb
  //   21e76b 21e72d 21e76e 21e7ee 21e723 21e7ef 21e72f 2121e7 212121 2121cb 21216b 21212d 21216e 2121ee
  //   212123 2121ef 21212f 21cbe7 21cb21 21cbcb 21cb6b 21cb2d 21cb6e 21cbee 21cb23 21cbef 21cb2f 216be7
  //   216b21 216bcb 216b6b 216b2d 216b6e 216bee 216b23 216bef 216b2f 212de7 212d21 212dcb 212d6b 212d2d
  //   212d6e 212dee 212d23 212def 212d2f 216ee7 216e21 216ecb 216e6b 216e2d 216e6e 216eee 216e23 216eef
  //   216e2f 21eee7 21ee21 21eecb 21ee6b 21ee2d 21ee6e 21eeee 21ee23 21eeef 21ee2f 2123e7 212321 2123cb
  //   21236b 21232d 21236e 2123ee 212323 2123ef 21232f 21efe7 21ef21 21efcb 21ef6b 21ef2d 21ef6e 21efee
  //   21ef23 21efef 21ef2f 212fe7 212f21 212fcb 212f6b 212f2d 212f6e 212fee 212f23 212fef 212f2f cbe7e7
  //   cbe721 cbe7cb cbe76b cbe72d cbe76e cbe7ee cbe723 cbe7ef cbe72f cb21e7 cb2121 cb21cb cb216b cb212d
  //   cb216e cb21ee cb2123 cb21ef cb212f cbcbe7 cbcb21 cbcbcb cbcb6b cbcb2d cbcb6e cbcbee cbcb23 cbcbef
  //   cbcb2f cb6be7 cb6b21 cb6bcb cb6b6b cb6b2d cb6b6e cb6bee cb6b23 cb6bef cb6b2f cb2de7 cb2d21 cb2dcb
  //   cb2d6b cb2d2d cb2d6e cb2dee cb2d23 cb2def cb2d2f cb6ee7 cb6e21 cb6ecb cb6e6b cb6e2d cb6e6e
  //   contents of rom_2 (hex, n*v repeats v):
  //   e7 21 cb 6b 2d 6e ee 23 ef 2f 21e7 2121 21cb 216b 212d 216e 21ee 2123 21ef 212f cbe7 cb21 cbcb cb6b
  //   cb2d cb6e cbee cb23 cbef cb2f 6be7 6b21 6bcb 6b6b 6b2d 6b6e 6bee 6b23 6bef 6b2f 2de7 2d21 2dcb 2d6b
  //   2d2d 2d6e 2dee 2d23 2def 2d2f 6ee7 6e21 6ecb 6e6b 6e2d 6e6e 6eee 6e23 6eef 6e2f eee7 ee21 eecb ee6b
  //   ee2d ee6e eeee ee23 eeef ee2f 23e7 2321 23cb 236b 232d 236e 23ee 2323 23ef 232f efe7 ef21 efcb ef6b
  //   ef2d ef6e efee ef23 efef ef2f 2fe7 2f21 2fcb 2f6b 2f2d 2f6e 2fee 2f23 2fef 2f2f 21e7e7 21e721 21e7cb
  //   21e76b 21e72d 21e76e 21e7ee 21e723 21e7ef 21e72f 2121e7 212121 2121cb 21216b 21212d 21216e 2121ee
  //   212123 2121ef 21212f 21cbe7 21cb21 21cbcb 21cb6b 21cb2d 21cb6e 21cbee 21cb23 21cbef 21cb2f 216be7
  //   216b21 216bcb 216b6b 216b2d 216b6e 216bee 216b23 216bef 216b2f 212de7 212d21 212dcb 212d6b 212d2d
  //   212d6e 212dee 212d23 212def 212d2f 216ee7 216e21 216ecb 216e6b 216e2d 216e6e 216eee 216e23 216eef
  //   216e2f 21eee7 21ee21 21eecb 21ee6b 21ee2d 21ee6e 21eeee 21ee23 21eeef 21ee2f 2123e7 212321 2123cb
  //   21236b 21232d 21236e 2123ee 212323 2123ef 21232f 21efe7 21ef21 21efcb 21ef6b 21ef2d 21ef6e 21efee
  //   21ef23 21efef 21ef2f 212fe7 212f21 212fcb 212f6b 212f2d 212f6e 212fee 212f23 212fef 212f2f cbe7e7
  //   cbe721 cbe7cb cbe76b cbe72d cbe76e cbe7ee cbe723 cbe7ef cbe72f cb21e7 cb2121 cb21cb cb216b cb212d
  //   cb216e cb21ee cb2123 cb21ef cb212f cbcbe7 cbcb21 cbcbcb cbcb6b cbcb2d cbcb6e cbcbee cbcb23 cbcbef
  //   cbcb2f cb6be7 cb6b21 cb6bcb cb6b6b cb6b2d cb6b6e cb6bee cb6b23 cb6bef cb6b2f cb2de7 cb2d21 cb2dcb
  //   cb2d6b cb2d2d cb2d6e cb2dee cb2d23 cb2def cb2d2f cb6ee7 cb6e21 cb6ecb cb6e6b cb6e2d cb6e6e
  //   contents of rom_3 (hex, n*v repeats v):
  //   e7 21 cb 6b 2d 6e ee 23 ef 2f 21e7 2121 21cb 216b 212d 216e
  //   step counter
endmodule

module _7seg (
  input  [7:0] Din,
  output [31:0] out_2
);

  ROM #(.dataWidth(32)) rom_1 (
    .addr(Din),
    .data({out_2[31:28], out_2[15:12], out_2[27:24], out_2[11:8], out_2[23:20], out_2[7:4], out_2[19:16], out_2[3:0]}));  // open: sel

  // Notes on the sheet:
  //   contents of rom_1 (hex, n*v repeats v):
  //   e7 21 cb 6b 2d 6e ee 23 ef 2f 21e7 2121 21cb 216b 212d 216e 21ee 2123 21ef 212f cbe7 cb21 cbcb cb6b
  //   cb2d cb6e cbee cb23 cbef cb2f 6be7 6b21 6bcb 6b6b 6b2d 6b6e 6bee 6b23 6bef 6b2f 2de7 2d21 2dcb 2d6b
  //   2d2d 2d6e 2dee 2d23 2def 2d2f 6ee7 6e21 6ecb 6e6b 6e2d 6e6e 6eee 6e23 6eef 6e2f eee7 ee21 eecb ee6b
  //   ee2d ee6e eeee ee23 eeef ee2f 23e7 2321 23cb 236b 232d 236e 23ee 2323 23ef 232f efe7 ef21 efcb ef6b
  //   ef2d ef6e efee ef23 efef ef2f 2fe7 2f21 2fcb 2f6b 2f2d 2f6e 2fee 2f23 2fef 2f2f 21e7e7 21e721 21e7cb
  //   21e76b 21e72d 21e76e 21e7ee 21e723 21e7ef 21e72f 2121e7 212121 2121cb 21216b 21212d 21216e 2121ee
  //   212123 2121ef 21212f 21cbe7 21cb21 21cbcb 21cb6b 21cb2d 21cb6e 21cbee 21cb23 21cbef 21cb2f 216be7
  //   216b21 216bcb 216b6b 216b2d 216b6e 216bee 216b23 216bef 216b2f 212de7 212d21 212dcb 212d6b 212d2d
  //   212d6e 212dee 212d23 212def 212d2f 216ee7 216e21 216ecb 216e6b 216e2d 216e6e 216eee 216e23 216eef
  //   216e2f 21eee7 21ee21 21eecb 21ee6b 21ee2d 21ee6e 21eeee 21ee23 21eeef 21ee2f 2123e7 212321 2123cb
  //   21236b 21232d 21236e 2123ee 212323 2123ef 21232f 21efe7 21ef21 21efcb 21ef6b 21ef2d 21ef6e 21efee
  //   21ef23 21efef 21ef2f 212fe7 212f21 212fcb 212f6b 212f2d 212f6e 212fee 212f23 212fef 212f2f cbe7e7
  //   cbe721 cbe7cb cbe76b cbe72d cbe76e cbe7ee cbe723 cbe7ef cbe72f cb21e7 cb2121 cb21cb cb216b cb212d
  //   cb216e cb21ee cb2123 cb21ef cb212f cbcbe7 cbcb21 cbcbcb cbcb6b cbcb2d cbcb6e cbcbee cbcb23 cbcbef
  //   cbcb2f cb6be7 cb6b21 cb6bcb cb6b6b cb6b2d cb6b6e cb6bee cb6b23 cb6bef cb6b2f cb2de7 cb2d21 cb2dcb
  //   cb2d6b cb2d2d cb2d6e cb2dee cb2d23 cb2def cb2d2f cb6ee7 cb6e21 cb6ecb cb6e6b cb6e2d cb6e6e
endmodule

module cu1 (
  input  OPC3,
  input  OPC2,
  input  OPC1,
  input  OPC0,
  input  SC2,
  input  SC1,
  input  SC0,
  output C0,
  output C1,
  output C2,
  output C8,
  output C3,
  output C9,
  output C4,
  output C10,
  output C5,
  output C6,
  output C11,
  output C7
);

  wire and_1_out, and_2_out, and_3_out, and_4_out, and_5_out, and_6_out, and_7_out, and_8_out, and_9_out,
       and_10_out, and_11_out, and_12_out, and_13_out, and_14_out, and_15_out, and_16_out, and_17_out,
       and_18_out, and_22_out, and_23_out, and_24_out, and_25_out, and_26_out, and_27_out, and_28_out,
       and_29_out, and_32_out, and_33_out, and_34_out, and_35_out, and_36_out, and_37_out, and_38_out,
       and_39_out, and_40_out, and_41_out, and_42_out, and_43_out, and_44_out, and_45_out, and_46_out,
       and_47_out, and_48_out, and_49_out, and_50_out, and_51_out, and_52_out, and_53_out, and_54_out,
       and_55_out, and_56_out, and_57_out, not_1_out, not_2_out, not_3_out, not_4_out, not_5_out, not_6_out,
       not_7_out, not_8_out, not_9_out, not_10_out, not_11_out, not_12_out, not_13_out, not_14_out,
       not_15_out, not_16_out, not_17_out, not_18_out, not_19_out, not_20_out, not_21_out, not_22_out,
       not_23_out, not_24_out, not_25_out, not_26_out, not_27_out, not_28_out, not_29_out, not_30_out,
       not_31_out, not_32_out, not_33_out, not_34_out, not_35_out, not_36_out, not_37_out, not_38_out,
       not_39_out, not_40_out, not_41_out, not_42_out, not_43_out, not_44_out, or_2_out, or_6_out, or_7_out;

  not not_1 (not_1_out, SC2);
  not not_2 (not_2_out, SC1);
  not not_3 (not_3_out, SC2);
  not not_4 (not_4_out, SC1);
  and and_1 (and_1_out, OPC0, OPC0);
  not not_5 (not_5_out, SC1);
  not not_6 (not_6_out, SC0);
  not not_7 (not_7_out, SC2);
  not not_8 (not_8_out, SC1);
  not not_9 (not_9_out, OPC0);
  not not_10 (not_10_out, SC1);
  not not_11 (not_11_out, SC0);
  not not_12 (not_12_out, SC2);
  not not_13 (not_13_out, SC1);
  not not_14 (not_14_out, OPC0);
  not not_15 (not_15_out, SC1);
  not not_16 (not_16_out, SC0);
  not not_17 (not_17_out, SC2);
  not not_18 (not_18_out, OPC0);
  not not_19 (not_19_out, SC1);
  and and_2 (and_2_out, OPC0, OPC0);
  not not_20 (not_20_out, SC1);
  not not_21 (not_21_out, SC0);
  not not_22 (not_22_out, SC2);
  and and_3 (and_3_out, not_1_out, not_2_out);
  not not_23 (not_23_out, SC0);
  and and_4 (and_4_out, not_3_out, not_4_out);
  and and_5 (and_5_out, and_1_out, SC2);
  and and_6 (and_6_out, not_5_out, not_6_out);
  and and_7 (and_7_out, not_7_out, not_8_out);
  and and_8 (and_8_out, not_9_out, SC2);
  and and_9 (and_9_out, not_10_out, not_11_out);
  and and_10 (and_10_out, not_12_out, not_13_out);
  and and_11 (and_11_out, not_14_out, SC2);
  and and_12 (and_12_out, not_15_out, not_16_out);
  not not_24 (not_24_out, SC2);
  and and_13 (and_13_out, not_17_out, SC1);
  not not_25 (not_25_out, SC0);
  and and_14 (and_14_out, not_18_out, SC2);
  and and_15 (and_15_out, not_19_out, SC0);
  and and_16 (and_16_out, and_2_out, SC2);
  and and_17 (and_17_out, not_20_out, not_21_out);
  and and_18 (and_18_out, not_22_out, SC1);
  not not_26 (not_26_out, SC0);
  and and_19 (C0, and_3_out, not_23_out);
  and and_20 (C1, and_4_out, SC0);
  and and_21 (C2, and_5_out, and_6_out);
  and and_22 (and_22_out, and_7_out, SC0);
  and and_23 (and_23_out, and_8_out, and_9_out);
  and and_24 (and_24_out, and_10_out, SC0);
  and and_25 (and_25_out, and_11_out, and_12_out);
  and and_26 (and_26_out, OPC0, OPC0);
  and and_27 (and_27_out, not_24_out, SC0);
  and and_28 (and_28_out, and_13_out, not_25_out);
  and and_29 (and_29_out, and_14_out, and_15_out);
  and and_30 (C6, and_16_out, and_17_out);
  and and_31 (C7, and_18_out, not_26_out);
  or or_1 (C3, and_22_out, and_23_out);
  or or_2 (or_2_out, and_24_out, and_25_out);
  and and_32 (and_32_out, and_26_out, and_27_out);
  or or_3 (C5, and_28_out, and_29_out);
  or or_4 (C4, or_2_out, and_32_out);
  not not_27 (not_27_out, OPC0);
  and and_33 (and_33_out, not_27_out, not_28_out);
  not not_28 (not_28_out, SC2);
  and and_34 (and_34_out, SC1, SC0);
  and and_35 (and_35_out, OPC0, not_29_out);
  not not_29 (not_29_out, SC2);
  and and_36 (and_36_out, SC1, SC0);
  not not_30 (not_30_out, SC2);
  and and_37 (and_37_out, not_30_out, not_31_out);
  not not_31 (not_31_out, SC1);
  not not_32 (not_32_out, SC0);
  not not_33 (not_33_out, OPC0);
  and and_38 (and_38_out, not_33_out, not_34_out);
  not not_34 (not_34_out, SC2);
  and and_39 (and_39_out, SC1, SC0);
  not not_35 (not_35_out, SC2);
  not not_36 (not_36_out, SC2);
  and and_40 (and_40_out, not_36_out, not_37_out);
  not not_37 (not_37_out, SC1);
  not not_38 (not_38_out, OPC0);
  and and_41 (and_41_out, not_38_out, SC2);
  not not_39 (not_39_out, SC1);
  and and_42 (and_42_out, not_39_out, not_40_out);
  not not_40 (not_40_out, SC0);
  not not_41 (not_41_out, SC1);
  not not_42 (not_42_out, SC0);
  and and_43 (and_43_out, OPC0, not_43_out);
  not not_43 (not_43_out, OPC0);
  not not_44 (not_44_out, SC2);
  and and_44 (and_44_out, and_33_out, and_34_out);
  and and_45 (and_45_out, and_35_out, and_36_out);
  and and_46 (and_46_out, and_37_out, not_32_out);
  and and_47 (and_47_out, and_38_out, and_39_out);
  and and_48 (and_48_out, OPC0, not_35_out);
  and and_49 (and_49_out, SC1, SC0);
  and and_50 (and_50_out, and_40_out, SC0);
  and and_51 (and_51_out, and_41_out, and_42_out);
  and and_52 (and_52_out, OPC0, SC2);
  and and_53 (and_53_out, not_41_out, not_42_out);
  and and_54 (and_54_out, and_43_out, not_44_out);
  and and_55 (and_55_out, SC1, SC0);
  or or_5 (C8, and_44_out, and_45_out);
  or or_6 (or_6_out, and_46_out, and_47_out);
  and and_56 (and_56_out, and_48_out, and_49_out);
  or or_7 (or_7_out, and_50_out, and_51_out);
  and and_57 (and_57_out, and_52_out, and_53_out);
  and and_58 (C11, and_54_out, and_55_out);
  or or_8 (C9, or_6_out, and_56_out);
  or or_9 (C10, or_7_out, and_57_out);

  assign OPC1 = OPC0;
endmodule

module CU2 (
  input  OPC3,
  input  OPC2,
  input  OPC1,
  input  OPC0,
  input  SC2,
  input  SC1,
  input  SC0,
  output C12,
  output C13,
  output C14,
  output C15
);

  wire and_1_out, and_2_out, and_3_out, and_4_out, and_5_out, and_6_out, and_7_out, and_8_out, and_9_out,
       and_10_out, and_12_out, and_13_out, not_1_out, not_2_out, not_3_out, not_4_out, not_5_out, not_6_out,
       not_7_out, not_8_out;

  not not_1 (not_1_out, OPC1);
  not not_2 (not_2_out, OPC0);
  not not_3 (not_3_out, OPC1);
  and and_1 (and_1_out, OPC1, OPC0);
  not not_4 (not_4_out, SC2);
  not not_5 (not_5_out, OPC0);
  and and_2 (and_2_out, not_1_out, not_2_out);
  not not_6 (not_6_out, SC1);
  and and_3 (and_3_out, not_3_out, OPC0);
  not not_7 (not_7_out, SC1);
  and and_4 (and_4_out, and_1_out, not_4_out);
  and and_5 (and_5_out, SC1, SC0);
  and and_6 (and_6_out, OPC1, not_5_out);
  not not_8 (not_8_out, SC2);
  and and_7 (and_7_out, and_2_out, SC2);
  and and_8 (and_8_out, not_6_out, SC0);
  and and_9 (and_9_out, and_3_out, SC2);
  and and_10 (and_10_out, not_7_out, SC0);
  and and_11 (C14, and_4_out, and_5_out);
  and and_12 (and_12_out, and_6_out, not_8_out);
  and and_13 (and_13_out, SC1, SC0);
  and and_14 (C12, and_7_out, and_8_out);
  and and_15 (C13, and_9_out, and_10_out);
  and and_16 (C15, and_12_out, and_13_out);
endmodule
